// Logisim project SCANNER2.circ as structural Verilog: 1 circuit, main circuit main
module main (
);

  wire clk_out, digital_oscilloscope_1_p2, digital_oscilloscope_1_p3, digital_oscilloscope_1_p5,
       n74139_1_pin5, n74139_1_pin7, n74139_1_pin9, n74139_1_pin10, n74139_1_pin11, n74139_1_pin12,
       n74193_1_pin1, n74193_1_pin2, n74193_1_pin3, n74193_1_pin4, n74193_1_pin12, n74193_2_pin2,
       n74193_2_pin3, n74193_2_pin6, n74193_2_pin7;

  Clock clk (.out(clk_out));
  _74193 #(.ShowInternalStructure("true"), .VccGndPorts("true")) u_74193_1 (
    .pin1(n74193_1_pin1), .pin2(n74193_1_pin2), .pin3(n74193_1_pin3), .pin4(n74193_1_pin4), .pin5(clk_out),
    .pin8(n74193_1_pin1), .pin16(n74193_1_pin4), .pin15(n74193_1_pin1), .pin14(n74193_1_pin1),
    .pin12(n74193_1_pin12), .pin11(n74193_1_pin4), .pin10(n74193_1_pin1), .pin9(n74193_1_pin1));  // open: pin6, pin7, pin13
  // Digital_Oscilloscope #(.nState(30)) digital_oscilloscope_1: pin names not known; wires that end beside it: clk_out, digital_oscilloscope_1_p2, digital_oscilloscope_1_p3, n74193_1_pin2, digital_oscilloscope_1_p5
  _74193 #(.ShowInternalStructure("true"), .VccGndPorts("true")) u_74193_2 (
    .pin1(n74193_1_pin1), .pin2(n74193_2_pin2), .pin3(n74193_2_pin3), .pin4(n74193_1_pin4),
    .pin5(n74193_1_pin12), .pin6(n74193_2_pin6), .pin7(n74193_2_pin7), .pin8(n74193_1_pin1),
    .pin16(n74193_1_pin4), .pin15(n74193_1_pin1), .pin14(n74193_1_pin1), .pin11(n74193_1_pin4),
    .pin10(n74193_1_pin1), .pin9(n74193_1_pin1));  // open: pin13, pin12
  nand nand_1 (digital_oscilloscope_1_p5, n74193_2_pin2, n74193_2_pin3);
  _74139 #(.ShowInternalStructure("true")) u_74139_1 (
    .pin1(digital_oscilloscope_1_p5), .pin2(n74193_1_pin3), .pin3(n74193_1_pin2),
    .pin4(digital_oscilloscope_1_p2), .pin5(n74139_1_pin5), .pin6(digital_oscilloscope_1_p3),
    .pin7(n74139_1_pin7), .pin15(n74193_1_pin1), .pin14(n74193_2_pin6), .pin13(n74193_2_pin7),
    .pin12(n74139_1_pin12), .pin11(n74139_1_pin11), .pin10(n74139_1_pin10), .pin9(n74139_1_pin9));
  // also tied to GND on the sheet: n74193_1_pin1
  // also tied to VCC on the sheet: n74193_1_pin4

  // Notes on the sheet:
  //   S1
  //   S2
  //   A0
  //   OE
endmodule
