// Logisim project SCANNER3.circ as structural Verilog: 1 circuit, main circuit main
module main (
);

  wire clk_out, digital_oscilloscope_1_p2, digital_oscilloscope_1_p3, digital_oscilloscope_1_p5,
       digital_oscilloscope_1_p6, digital_oscilloscope_1_p7, digital_oscilloscope_1_p8,
       digital_oscilloscope_1_p9, n74139_1_pin5, n74139_1_pin7, n74193_1_pin1, n74193_1_pin3, n74193_1_pin4,
       n74193_1_pin6, n74193_1_pin7, n74193_1_pin12, n74193_2_pin2, n74193_2_pin3, not_1_out, not_2_out,
       not_3_out, not_4_out, not_5_out, not_6_out, not_7_out;
  wire [2:0] n74193_1_pin2;
  wire [3:0] and_1_out;
  wire [7:0] register_2_q, rom_1_data;

  Clock clk (.out(clk_out));
  _74193 #(.ShowInternalStructure("true"), .VccGndPorts("true")) u_74193_1 (
    .pin1(n74193_1_pin1), .pin2(n74193_1_pin2[0]), .pin3(n74193_1_pin3), .pin4(n74193_1_pin4),
    .pin5(clk_out), .pin6(n74193_1_pin6), .pin7(n74193_1_pin7), .pin8(n74193_1_pin1), .pin16(n74193_1_pin4),
    .pin15(n74193_1_pin1), .pin14(n74193_1_pin1), .pin12(n74193_1_pin12), .pin11(n74193_1_pin4),
    .pin10(n74193_1_pin1), .pin9(n74193_1_pin1));  // open: pin13
  // Digital_Oscilloscope #(.nState(35)) digital_oscilloscope_1: pin names not known; wires that end beside it: clk_out, digital_oscilloscope_1_p2, digital_oscilloscope_1_p3, n74193_1_pin2[0], digital_oscilloscope_1_p5, digital_oscilloscope_1_p6, digital_oscilloscope_1_p7, digital_oscilloscope_1_p8, digital_oscilloscope_1_p9
  _74193 #(.ShowInternalStructure("true"), .VccGndPorts("true")) u_74193_2 (
    .pin1(n74193_1_pin1), .pin2(n74193_2_pin2), .pin3(n74193_2_pin3), .pin4(n74193_1_pin4),
    .pin5(n74193_1_pin12), .pin6(n74193_1_pin2[1]), .pin7(n74193_1_pin2[2]), .pin8(n74193_1_pin1),
    .pin16(n74193_1_pin4), .pin15(n74193_1_pin1), .pin14(n74193_1_pin1), .pin11(n74193_1_pin4),
    .pin10(n74193_1_pin1), .pin9(n74193_1_pin1));  // open: pin13, pin12
  nand nand_1 (digital_oscilloscope_1_p5, n74193_2_pin3, n74193_1_pin7, n74193_1_pin6, n74193_2_pin2);
  not not_1 (not_1_out, digital_oscilloscope_1_p5);
  _74139 #(.ShowInternalStructure("true")) u_74139_1 (
    .pin1(digital_oscilloscope_1_p5), .pin2(n74193_1_pin3), .pin3(n74193_1_pin2[0]),
    .pin4(digital_oscilloscope_1_p2), .pin5(n74139_1_pin5), .pin6(digital_oscilloscope_1_p3),
    .pin7(n74139_1_pin7), .pin15(not_1_out), .pin14(n74193_1_pin2[1]), .pin13(n74193_1_pin2[2]),
    .pin12(digital_oscilloscope_1_p6), .pin11(digital_oscilloscope_1_p7), .pin10(digital_oscilloscope_1_p8),
    .pin9(digital_oscilloscope_1_p9));
  ROM rom_1 (.addr({{5{1'b0}}, n74193_1_pin2}), .data(rom_1_data));
  not not_2 (not_2_out, digital_oscilloscope_1_p2);
  not not_3 (not_3_out, digital_oscilloscope_1_p3);
  Register register_1 (.D(rom_1_data), .en(n74193_1_pin4), .clk(not_2_out));  // open: Q, clr
  Register register_2 (.D(rom_1_data), .en(n74193_1_pin4), .clk(not_3_out), .Q(register_2_q));  // open: clr
  not not_4 (not_4_out, digital_oscilloscope_1_p6);
  not not_5 (not_5_out, digital_oscilloscope_1_p7);
  not not_6 (not_6_out, digital_oscilloscope_1_p8);
  not not_7 (not_7_out, digital_oscilloscope_1_p9);
  and and_1 (and_1_out[0], not_4_out, digital_oscilloscope_1_p5);
  and and_2 (and_1_out[1], not_5_out, digital_oscilloscope_1_p5);
  and and_3 (and_1_out[2], not_6_out, digital_oscilloscope_1_p5);
  and and_4 (and_1_out[3], not_7_out, digital_oscilloscope_1_p5);
  // DotMatrix #(.dotshape("circle"), .inputtype("select"), .matrixcols(4), .matrixrows(8)) dotmatrix_1: pin names not known; wires that end beside it: register_2_q, and_1_out, register_2_q
  // also tied to GND on the sheet: n74193_1_pin1
  // also tied to VCC on the sheet: n74193_1_pin4

  // Notes on the sheet:
  //   S1
  //   S2
  //   A0
  //   OE
  //   DIGIT0
  //   DIGIT1
  //   DIGIT2
  //   DIGIT3
  //   A2
  //   A1
  //   contents of rom_1 (hex, n*v repeats v):
  //   55 aa ff 0 11 22 44 88 8*0 22
endmodule
